// Logisim project vertebrate.circ as structural Verilog: 26 circuits, main circuit Simulation
module CPU (
  input  [15:0] din,
  input  clk,
  input  INT,
  output MEMLD,
  output INTACK,
  output [15:0] Dout,
  output [11:0] Addrout
);

  wire ALUz, INTLD, IRLD, multiplexer_1_out, MUX, or_1_out, PCINC, PCLD, PCMUX, REGLD, SP_minus, SP_plus, Z,
       ZFLD, ZFPOP;
  wire [1:0] ARMUX, DATAMUX;
  wire [2:0] DR, SR1, SR2;
  wire [3:0] ALUC;
  wire [11:0] adder_1_out, instr, ISR, multiplexer_2_out, PC;
  wire [15:0] ALUout, bit_extender_1_out, bit_extender_2_out, multiplexer_3_out, R1, R2, SP;

  ALU alu_1 (.op1(R1), .op2(R2), .ALUC(ALUC), .ALUz(ALUz), .ALUout(ALUout));
  Instruction_Decoder instruction_decoder_1 (.instr(instr), .dr(DR), .sr1(SR1), .sr2(SR2), .ALUC(ALUC));
  IR ir_1 (.ld(din[11:0]), .en(IRLD), .clk(clk), .rd(instr));
  or or_1 (or_1_out, ZFLD, ZFPOP);
  Multiplexer #(.enable("false")) multiplexer_1 (.in0(din[0]), .in1(ALUz), .out(multiplexer_1_out), .sel(ZFLD));
  ZF zf_1 (.ld(multiplexer_1_out), .en(or_1_out), .clk(clk), .rd(Z));
  Adder #(.width(12)) adder_1 (.a(instr), .b(PC), .out(adder_1_out));  // open: cin, cout
  Multiplexer #(.width(12), .enable("false")) multiplexer_2 (
    .in0(adder_1_out), .in1(din[11:0]), .out(multiplexer_2_out), .sel(PCMUX));
  Multiplexer #(.width(16), .enable("false")) multiplexer_3 (
    .in0(ALUout), .in1(din), .out(multiplexer_3_out), .sel(MUX));
  PC pc_1 (.ld(multiplexer_2_out), .PCLD(PCLD), .PCINC(PCINC), .clk(clk), .rd(PC));
  Interrupt_Register interrupt_register_1 (.INTV(din[2:0]), .INTLD(INTLD), .clk(clk), .ISR(ISR));
  Register_File register_file_1 (
    .ld(multiplexer_3_out), .clk(clk), .sr1(SR1), .sr2(SR2), .R1(R1), .R2(R2), .sw(DR), .en(REGLD), .SP(SP),
    .SP_plus(SP_plus), .SP_minus(SP_minus));
  Control_Unit control_unit_1 (
    .Z(Z), .opc(din[15:12]), .clk(clk), .INT(INT), .INTACK(INTACK), .DATAMUX(DATAMUX), .ARMUX(ARMUX),
    .PCMUX(PCMUX), .MUX(MUX), .PCINC(PCINC), .SP_plus(SP_plus), .SP_minus(SP_minus), .ZFPOP(ZFPOP),
    .ZFLD(ZFLD), .INTLD(INTLD), .MEMLD(MEMLD), .REGLD(REGLD), .PCLD(PCLD), .IRLD(IRLD));
  assign bit_extender_1_out = {{4{1'b0}}, PC};  // Bit_Extender bit_extender_1
  Multiplexer #(.select(2), .width(16), .enable("false")) multiplexer_4 (
    .in0(R2), .in1(bit_extender_1_out), .in2(bit_extender_2_out), .out(Dout), .sel(DATAMUX));  // open: in3
  assign bit_extender_2_out = {{15{1'b0}}, Z};  // Bit_Extender bit_extender_2
  Multiplexer #(.select(2), .width(12), .enable("false")) multiplexer_5 (
    .in0(PC), .in1(R1[11:0]), .in2(SP[11:0]), .in3(ISR), .out(Addrout), .sel(ARMUX));

  // Notes on the sheet:
  //   Input
  //   Output
endmodule

module ALU (
  input  [15:0] op1,
  input  [15:0] op2,
  input  [3:0] ALUC,
  output [15:0] ALUout,
  output ALUz
);

  wire and_1_out, and_2_out, and_3_out, and_4_out, and_5_out, and_6_out, and_7_out, and_8_out, and_9_out,
       and_10_out, and_11_out, and_12_out, and_13_out;
  wire [0:0] or_4_out;
  wire [2:0] or_3_out;
  wire [15:0] adder_1_out, and_14_out, clz_16_1_q, multiplexer_1_out, multiplexer_2_out, not_1_out,
       not_2_out, or_5_out, shifter_1_out, shifter_2_out, xor_1_out;

  and and_1 (and_1_out, ~ALUC[3], ~ALUC[2], ~ALUC[1], ALUC[0]);  // AND_Gate
  and and_2 (and_2_out, ALUC[2], ALUC[0]);
  and and_3 (and_3_out, ALUC[2], ALUC[1]);
  or or_1 (or_3_out[2], and_2_out, and_3_out, and_4_out);
  and and_4 (and_4_out, ALUC[3], ~ALUC[1]);  // AND_Gate
  and and_5 (and_5_out, ~ALUC[3], ALUC[1], ALUC[0]);  // AND_Gate
  or or_2 (or_3_out[1], and_5_out, and_6_out, and_7_out);
  and and_6 (and_6_out, ALUC[2], ~ALUC[1], ~ALUC[0]);  // AND_Gate
  and and_7 (and_7_out, ALUC[3], ~ALUC[1]);  // AND_Gate
  and and_8 (and_8_out, ~ALUC[3], ALUC[1], ~ALUC[0]);  // AND_Gate
  or or_3 (or_3_out[0], and_8_out, and_9_out, and_10_out);
  and and_9 (and_9_out, ALUC[2], ~ALUC[0]);  // AND_Gate
  and and_10 (and_10_out, ALUC[3], ~ALUC[1], ALUC[0]);  // AND_Gate
  and and_11 (and_11_out, ~ALUC[2], ~ALUC[1], ALUC[0]);  // AND_Gate
  or or_4 (or_4_out[0], and_11_out, and_12_out);
  and and_12 (and_12_out, ALUC[3], ALUC[0]);
  and and_13 (and_13_out, ~ALUC[0], ~ALUC[1], ALUC[2], ALUC[3]);  // AND_Gate
  assign not_1_out = ~op2;  // NOT_Gate not_1, 16 bits wide
  Multiplexer #(.select(2), .width(16), .enable("false")) multiplexer_1 (
    .in0(op2), .in1(not_1_out), .in2(16'h1), .in3({16{1'b1}}), .out(multiplexer_1_out),
    .sel({ALUC[3], or_4_out[0]}));
  Adder #(.width(16)) adder_1 (.a(op1), .b(multiplexer_1_out), .out(adder_1_out), .cin(and_1_out));  // open: cout
  assign and_14_out = op1 & multiplexer_1_out;  // AND_Gate and_14, 16 bits wide
  assign or_5_out = op1 | multiplexer_1_out;  // OR_Gate or_5, 16 bits wide
  assign xor_1_out = op1 ^ multiplexer_1_out;  // XOR_Gate xor_1, 16 bits wide
  Shifter #(.width(16)) shifter_1 (.in(op1), .\dist (multiplexer_1_out[3:0]), .out(shifter_1_out));
  Shifter #(.width(16), .shift("lr")) shifter_2 (.in(op1), .\dist (multiplexer_1_out[3:0]), .out(shifter_2_out));
  assign not_2_out = ~op1;  // NOT_Gate not_2, 16 bits wide
  clz_16 clz_16_1 (.D(op1), .Q(clz_16_1_q));
  Multiplexer #(.select(3), .width(16), .enable("false")) multiplexer_2 (
    .in0(adder_1_out), .in1(and_14_out), .in2(or_5_out), .in3(xor_1_out), .in4(shifter_1_out),
    .in5(shifter_2_out), .in6(op1), .in7(not_2_out), .out(multiplexer_2_out), .sel(or_3_out));
  Multiplexer #(.width(16), .enable("false")) multiplexer_3 (
    .in0(multiplexer_2_out), .in1(clz_16_1_q), .out(ALUout), .sel(and_13_out));
  nor nor_1 (ALUz, ALUout[0], ALUout[1], ALUout[2], ALUout[3], ALUout[4], ALUout[5], ALUout[6], ALUout[7], ALUout[8], ALUout[9], ALUout[10], ALUout[11], ALUout[12], ALUout[13], ALUout[14], ALUout[15]);
endmodule

module PC (
  input  [11:0] ld,
  input  PCLD,
  input  PCINC,
  input  clk,
  output [11:0] rd
);

  wire or_1_out;
  wire [11:0] adder_1_out, multiplexer_1_out;

  Multiplexer #(.width(12), .enable("false")) multiplexer_1 (
    .in0(adder_1_out), .in1(ld), .out(multiplexer_1_out), .sel(PCLD));
  Register_12 register_12_1 (.ld(multiplexer_1_out), .en(or_1_out), .clk(clk), .rd(rd));
  or or_1 (or_1_out, PCLD, PCINC);
  Adder #(.width(12)) adder_1 (.a(12'h1), .b(rd), .out(adder_1_out));  // open: cin, cout
endmodule

module Register_File (
  input  en,
  input  [2:0] sw,
  input  [15:0] ld,
  input  SP_plus,
  input  SP_minus,
  input  clk,
  input  [2:0] sr1,
  input  [2:0] sr2,
  output [15:0] R1,
  output [15:0] SP,
  output [15:0] R2
);

  wire demultiplexer_1_out0, demultiplexer_1_out1, demultiplexer_1_out2, demultiplexer_1_out3,
       demultiplexer_1_out4, demultiplexer_1_out5, demultiplexer_1_out6, demultiplexer_1_out7, or_1_out,
       or_2_out;
  wire [15:0] adder_1_out, multiplexer_1_out, multiplexer_2_out, register_16_2_rd, register_16_3_rd,
       register_16_4_rd, register_16_5_rd, register_16_6_rd, register_16_7_rd, register_16_8_rd;

  Multiplexer #(.width(16), .enable("false")) multiplexer_1 (
    .in0({16{1'b1}}), .in1(16'h1), .out(multiplexer_1_out), .sel(SP_plus));
  Adder #(.width(16)) adder_1 (.a(multiplexer_1_out), .b(SP), .out(adder_1_out));  // open: cin, cout
  or or_1 (or_1_out, SP_plus, SP_minus);
  Multiplexer #(.width(16), .enable("false")) multiplexer_2 (
    .in0(ld), .in1(adder_1_out), .out(multiplexer_2_out), .sel(or_1_out));
  or or_2 (or_2_out, demultiplexer_1_out7, or_1_out);
  Register_16 register_16_1 (.ld(multiplexer_2_out), .en(or_2_out), .clk(clk), .rd(SP));
  Register_16 register_16_2 (.ld(ld), .en(demultiplexer_1_out6), .clk(clk), .rd(register_16_2_rd));
  Multiplexer #(.select(3), .width(16), .enable("false")) multiplexer_3 (
    .in0(register_16_8_rd), .in1(register_16_7_rd), .in2(register_16_6_rd), .in3(register_16_5_rd),
    .in4(register_16_4_rd), .in5(register_16_3_rd), .in6(register_16_2_rd), .in7(SP), .out(R1), .sel(sr1));
  Register_16 register_16_3 (.ld(ld), .en(demultiplexer_1_out5), .clk(clk), .rd(register_16_3_rd));
  Register_16 register_16_4 (.ld(ld), .en(demultiplexer_1_out4), .clk(clk), .rd(register_16_4_rd));
  Demultiplexer #(.select(3), .enable("false")) demultiplexer_1 (
    .out0(demultiplexer_1_out0), .out1(demultiplexer_1_out1), .out2(demultiplexer_1_out2),
    .out3(demultiplexer_1_out3), .out4(demultiplexer_1_out4), .out5(demultiplexer_1_out5),
    .out6(demultiplexer_1_out6), .out7(demultiplexer_1_out7), .in(en), .sel(sw));
  Register_16 register_16_5 (.ld(ld), .en(demultiplexer_1_out3), .clk(clk), .rd(register_16_5_rd));
  Register_16 register_16_6 (.ld(ld), .en(demultiplexer_1_out2), .clk(clk), .rd(register_16_6_rd));
  Register_16 register_16_7 (.ld(ld), .en(demultiplexer_1_out1), .clk(clk), .rd(register_16_7_rd));
  Register_16 register_16_8 (.ld(ld), .en(demultiplexer_1_out0), .clk(clk), .rd(register_16_8_rd));
  Multiplexer #(.select(3), .width(16), .enable("false")) multiplexer_4 (
    .in0(register_16_8_rd), .in1(register_16_7_rd), .in2(register_16_6_rd), .in3(register_16_5_rd),
    .in4(register_16_4_rd), .in5(register_16_3_rd), .in6(register_16_2_rd), .in7(SP), .out(R2), .sel(sr2));
endmodule

module Register_12 (
  input  [11:0] ld,
  input  en,
  input  clk,
  output [11:0] rd
);

  D_Flip_Flop d_ff_1 (.D(ld[11]), .clk(clk), .Q(rd[11]), .en(en));  // open: clr
  D_Flip_Flop d_ff_2 (.D(ld[10]), .clk(clk), .Q(rd[10]), .en(en));  // open: clr
  D_Flip_Flop d_ff_3 (.D(ld[9]), .clk(clk), .Q(rd[9]), .en(en));  // open: clr
  D_Flip_Flop d_ff_4 (.D(ld[8]), .clk(clk), .Q(rd[8]), .en(en));  // open: clr
  D_Flip_Flop d_ff_5 (.D(ld[6]), .clk(clk), .Q(rd[6]), .en(en));  // open: clr
  D_Flip_Flop d_ff_6 (.D(ld[7]), .clk(clk), .Q(rd[7]), .en(en));  // open: clr
  D_Flip_Flop d_ff_7 (.D(ld[5]), .clk(clk), .Q(rd[5]), .en(en));  // open: clr
  D_Flip_Flop d_ff_8 (.D(ld[4]), .clk(clk), .Q(rd[4]), .en(en));  // open: clr
  D_Flip_Flop d_ff_9 (.D(ld[3]), .clk(clk), .Q(rd[3]), .en(en));  // open: clr
  D_Flip_Flop d_ff_10 (.D(ld[2]), .clk(clk), .Q(rd[2]), .en(en));  // open: clr
  D_Flip_Flop d_ff_11 (.D(ld[1]), .clk(clk), .Q(rd[1]), .en(en));  // open: clr
  D_Flip_Flop d_ff_12 (.D(ld[0]), .clk(clk), .Q(rd[0]), .en(en));  // open: clr
endmodule

module Register_16 (
  input  [15:0] ld,
  input  en,
  input  clk,
  output [15:0] rd
);

  D_Flip_Flop d_ff_1 (.D(ld[14]), .clk(clk), .Q(rd[14]), .en(en));  // open: clr
  D_Flip_Flop d_ff_2 (.D(ld[15]), .clk(clk), .Q(rd[15]), .en(en));  // open: clr
  D_Flip_Flop d_ff_3 (.D(ld[13]), .clk(clk), .Q(rd[13]), .en(en));  // open: clr
  D_Flip_Flop d_ff_4 (.D(ld[12]), .clk(clk), .Q(rd[12]), .en(en));  // open: clr
  D_Flip_Flop d_ff_5 (.D(ld[11]), .clk(clk), .Q(rd[11]), .en(en));  // open: clr
  D_Flip_Flop d_ff_6 (.D(ld[10]), .clk(clk), .Q(rd[10]), .en(en));  // open: clr
  D_Flip_Flop d_ff_7 (.D(ld[9]), .clk(clk), .Q(rd[9]), .en(en));  // open: clr
  D_Flip_Flop d_ff_8 (.D(ld[8]), .clk(clk), .Q(rd[8]), .en(en));  // open: clr
  D_Flip_Flop d_ff_9 (.D(ld[7]), .clk(clk), .Q(rd[7]), .en(en));  // open: clr
  D_Flip_Flop d_ff_10 (.D(ld[5]), .clk(clk), .Q(rd[5]), .en(en));  // open: clr
  D_Flip_Flop d_ff_11 (.D(ld[6]), .clk(clk), .Q(rd[6]), .en(en));  // open: clr
  D_Flip_Flop d_ff_12 (.D(ld[4]), .clk(clk), .Q(rd[4]), .en(en));  // open: clr
  D_Flip_Flop d_ff_13 (.D(ld[3]), .clk(clk), .Q(rd[3]), .en(en));  // open: clr
  D_Flip_Flop d_ff_14 (.D(ld[2]), .clk(clk), .Q(rd[2]), .en(en));  // open: clr
  D_Flip_Flop d_ff_15 (.D(ld[1]), .clk(clk), .Q(rd[1]), .en(en));  // open: clr
  D_Flip_Flop d_ff_16 (.D(ld[0]), .clk(clk), .Q(rd[0]), .en(en));  // open: clr
endmodule

module D_Flip_Flop (
  input  D,
  input  clk,
  input  en,
  input  clr,
  output Q
);

  wire not_1_out;

  not not_1 (not_1_out, D);
  S_R_Flip_Flop_part s_r_ff_1 (.S(D), .clk(clk), .R(not_1_out), .Q(Q), .reset(clr), .en(en));  // open: Qn, preset
endmodule

module Instruction_Decoder (
  input  [11:0] instr,
  output [2:0] dr,
  output [2:0] sr1,
  output [2:0] sr2,
  output [3:0] ALUC
);

  wire and_1_out;
  wire [3:0] bit_extender_1_out;

  and and_1 (and_1_out, instr[9], instr[10], instr[11]);
  assign bit_extender_1_out = {{1{1'b0}}, instr[11:9]};  // Bit_Extender bit_extender_1
  Multiplexer #(.width(4), .enable("false")) multiplexer_1 (
    .in0(bit_extender_1_out), .in1(instr[9:6]), .out(ALUC), .sel(and_1_out));

  assign dr = instr[2:0];
  assign sr1 = instr[5:3];
  assign sr2 = instr[8:6];
endmodule

module IR (
  input  [11:0] ld,
  input  en,
  input  clk,
  output [11:0] rd
);

  Register_12 register_12_1 (.ld(ld), .en(en), .clk(clk), .rd(rd));
endmodule

module ZF (
  input  ld,
  input  en,
  input  clk,
  output rd
);

  D_Flip_Flop d_ff_1 (.D(ld), .clk(clk), .Q(rd), .en(en));  // open: clr
endmodule

module Simulation (
  input  PB2,
  input  [3:0] SWB
);

  wire and_1_out, and_2_out, and_3_out, and_4_out, and_5_out, and_6_out, and_7_out, and_8_out, and_9_out,
       and_10_out, clock_1_out, cpu_1_intack, cpu_1_memld, PB1_out, PIC_int, pull_resistor_1_node, Timer_irq;
  wire [2:0] n4_7_segment_adapter_1_edc1, n4_7_segment_adapter_1_edc2, n4_7_segment_adapter_1_edc3,
       n4_7_segment_adapter_1_edc4, PIC_intv;
  wire [3:0] n4_7_segment_adapter_1_gfab1, n4_7_segment_adapter_1_gfab2, n4_7_segment_adapter_1_gfab3,
       n4_7_segment_adapter_1_gfab4;
  wire [11:0] cpu_1_addrout;
  wire [15:0] bit_extender_1_out, cpu_1_dout, multiplexer_1_out, multiplexer_2_out, multiplexer_3_out,
       multiplexer_4_out, multiplexer_5_out, multiplexer_6_out, n4_7_segment_adapter_1_rd, ram_1_data,
       switch_adapter_1_rd, switch_adapter_with_memory_1_rd, switchboard_4_adapter_1_rd, Timer_t;

  Clock clock_1 (.out(clock_1_out));
  Timer Timer (.t(Timer_t), .IRQ(Timer_irq));
  CPU cpu_1 (
    .din(multiplexer_6_out), .clk(clock_1_out), .MEMLD(cpu_1_memld), .Addrout(cpu_1_addrout),
    .Dout(cpu_1_dout), .INT(PIC_int), .INTACK(cpu_1_intack));
  Interrupt_Controller PIC (
    .IRQ0(Timer_irq), .INTV(PIC_intv), .INTACK(cpu_1_intack), .INT(PIC_int));  // open: IRQ1, IRQ2, IRQ3, IRQ4, IRQ5, IRQ6, IRQ7
  assign bit_extender_1_out = {{13{1'b0}}, PIC_intv};  // Bit_Extender bit_extender_1
  and and_1 (and_1_out, cpu_1_addrout[4], cpu_1_addrout[5], cpu_1_addrout[6], cpu_1_addrout[7], cpu_1_addrout[8], cpu_1_addrout[9], cpu_1_addrout[10], ~cpu_1_addrout[11]);  // AND_Gate
  and and_2 (and_2_out, ~cpu_1_addrout[0], ~cpu_1_addrout[1], ~cpu_1_addrout[2], ~cpu_1_addrout[3], ~cpu_1_addrout[4], ~cpu_1_addrout[5], ~cpu_1_addrout[6], ~cpu_1_addrout[7], ~cpu_1_addrout[8], ~cpu_1_addrout[9], ~cpu_1_addrout[10], cpu_1_addrout[11]);  // AND_Gate
  Switch_Adapter_With_Memory switch_adapter_with_memory_1 (
    .en(and_3_out), .addr(cpu_1_addrout[0]), .ldsr(cpu_1_dout), .clk(clock_1_out), .lddr(PB1_out),
    .rd(switch_adapter_with_memory_1_rd));
  and and_3 (and_3_out, and_4_out, cpu_1_memld);
  and and_4 (and_4_out, cpu_1_addrout[3], ~cpu_1_addrout[2], ~cpu_1_addrout[1], and_1_out);  // AND_Gate
  and and_5 (and_5_out, cpu_1_addrout[3], ~cpu_1_addrout[2], cpu_1_addrout[1], and_1_out);  // AND_Gate
  and and_6 (and_6_out, cpu_1_addrout[3], cpu_1_addrout[2], ~cpu_1_addrout[1], and_1_out);  // AND_Gate
  and and_7 (and_7_out, cpu_1_addrout[3], cpu_1_addrout[2], cpu_1_addrout[1], and_1_out);
  Switch_Adapter switch_adapter_1 (
    .addr(cpu_1_addrout[0]), .ldsr(cpu_1_dout), .lddr(PB2), .clk(clock_1_out), .rd(switch_adapter_1_rd),
    .en(and_8_out));
  and and_8 (and_8_out, and_5_out, cpu_1_memld);
  Button PB1 (.out(PB1_out));
  SwitchBoard_4_Adapter switchboard_4_adapter_1 (
    .addr(cpu_1_addrout[0]), .ldsr(cpu_1_dout), .lddr(SWB), .clk(clock_1_out),
    .rd(switchboard_4_adapter_1_rd), .en(and_9_out));
  and and_9 (and_9_out, and_6_out, cpu_1_memld);
  _7_Segment_Display u_7_segment_display_1 (
    .g(n4_7_segment_adapter_1_gfab4[3]), .f(n4_7_segment_adapter_1_gfab4[2]),
    .a(n4_7_segment_adapter_1_gfab4[1]), .b(n4_7_segment_adapter_1_gfab4[0]),
    .e(n4_7_segment_adapter_1_edc4[2]), .d(n4_7_segment_adapter_1_edc4[1]), .c(n4_7_segment_adapter_1_edc4[0]));  // open: dp
  _7_Segment_Display u_7_segment_display_2 (
    .g(n4_7_segment_adapter_1_gfab3[3]), .f(n4_7_segment_adapter_1_gfab3[2]),
    .a(n4_7_segment_adapter_1_gfab3[1]), .b(n4_7_segment_adapter_1_gfab3[0]),
    .e(n4_7_segment_adapter_1_edc3[2]), .d(n4_7_segment_adapter_1_edc3[1]), .c(n4_7_segment_adapter_1_edc3[0]));  // open: dp
  _7_Segment_Display u_7_segment_display_3 (
    .g(n4_7_segment_adapter_1_gfab2[3]), .f(n4_7_segment_adapter_1_gfab2[2]),
    .a(n4_7_segment_adapter_1_gfab2[1]), .b(n4_7_segment_adapter_1_gfab2[0]),
    .e(n4_7_segment_adapter_1_edc2[2]), .d(n4_7_segment_adapter_1_edc2[1]), .c(n4_7_segment_adapter_1_edc2[0]));  // open: dp
  _4_7_Segment_Adapter u_4_7_segment_adapter_1 (
    .edc1(n4_7_segment_adapter_1_edc1), .gfab2(n4_7_segment_adapter_1_gfab2), .ld(cpu_1_dout),
    .clk(clock_1_out), .addr(cpu_1_addrout[0]), .rd(n4_7_segment_adapter_1_rd), .en(and_10_out),
    .gfab1(n4_7_segment_adapter_1_gfab1), .edc2(n4_7_segment_adapter_1_edc2),
    .gfab3(n4_7_segment_adapter_1_gfab3), .edc3(n4_7_segment_adapter_1_edc3),
    .gfab4(n4_7_segment_adapter_1_gfab4), .edc4(n4_7_segment_adapter_1_edc4));
  and and_10 (and_10_out, and_7_out, cpu_1_memld);
  _7_Segment_Display u_7_segment_display_4 (
    .g(n4_7_segment_adapter_1_gfab1[3]), .f(n4_7_segment_adapter_1_gfab1[2]),
    .a(n4_7_segment_adapter_1_gfab1[1]), .b(n4_7_segment_adapter_1_gfab1[0]),
    .e(n4_7_segment_adapter_1_edc1[2]), .d(n4_7_segment_adapter_1_edc1[1]), .c(n4_7_segment_adapter_1_edc1[0]));  // open: dp
  RAM #(.addrWidth(12), .dataWidth(16), .bus("separate")) ram_1 (
    .addr(cpu_1_addrout), .din(cpu_1_dout), .data(ram_1_data), .str(cpu_1_memld), .sel(pull_resistor_1_node),
    .clk(clock_1_out), .ld(pull_resistor_1_node));  // open: clr
  Pull_Resistor #(.pull(1)) pull_resistor_1 (.node(pull_resistor_1_node));
  Multiplexer #(.width(16), .enable("false")) multiplexer_1 (
    .in0(ram_1_data), .in1(switch_adapter_with_memory_1_rd), .out(multiplexer_1_out), .sel(and_4_out));
  Multiplexer #(.width(16), .enable("false")) multiplexer_2 (
    .in0(multiplexer_1_out), .in1(switch_adapter_1_rd), .out(multiplexer_2_out), .sel(and_5_out));
  Multiplexer #(.width(16), .enable("false")) multiplexer_3 (
    .in0(multiplexer_2_out), .in1(switchboard_4_adapter_1_rd), .out(multiplexer_3_out), .sel(and_6_out));
  Multiplexer #(.width(16), .enable("false")) multiplexer_4 (
    .in0(multiplexer_3_out), .in1(n4_7_segment_adapter_1_rd), .out(multiplexer_4_out), .sel(and_7_out));
  Multiplexer #(.width(16), .enable("false")) multiplexer_5 (
    .in0(multiplexer_4_out), .in1(Timer_t), .out(multiplexer_5_out), .sel(and_2_out));
  Multiplexer #(.width(16), .enable("false")) multiplexer_6 (
    .in0(multiplexer_5_out), .in1(bit_extender_1_out), .out(multiplexer_6_out), .sel(cpu_1_intack));

  // Notes on the sheet:
  //   7-Segment Display
  //   RAM
endmodule

module Control_Unit (
  input  [3:0] opc,
  input  Z,
  input  INT,
  input  clk,
  output INTACK,
  output [1:0] DATAMUX,
  output [1:0] ARMUX,
  output PCMUX,
  output MUX,
  output PCINC,
  output SP_plus,
  output SP_minus,
  output ZFPOP,
  output ZFLD,
  output INTLD,
  output MEMLD,
  output REGLD,
  output PCLD,
  output IRLD
);

  wire and_1_out, and_2_out, and_3_out, and_4_out, and_5_out, pull_resistor_1_node, s_r_ff_1_q;
  wire [1:0] or_1_out;
  wire [4:0] bit_extender_1_out, multiplexer_1_out, register_5_1_rd;
  wire [23:16] rom_1_data;

  assign bit_extender_1_out = {{1{1'b0}}, opc};  // Bit_Extender bit_extender_1
  Multiplexer #(.select(2), .width(5), .enable("false")) multiplexer_1 (
    .in0({5{1'b0}}), .in1(bit_extender_1_out), .in2(rom_1_data[23:19]), .in3(5'b10011),
    .out(multiplexer_1_out), .sel(or_1_out));
  Register_5 register_5_1 (.ld(multiplexer_1_out), .en(pull_resistor_1_node), .clk(clk), .rd(register_5_1_rd));
  Pull_Resistor #(.pull(1)) pull_resistor_1 (.node(pull_resistor_1_node));
  and and_1 (and_1_out, ~opc[0], ~opc[1], opc[2], ~opc[3]);  // AND_Gate
  ROM #(.addrWidth(5), .dataWidth(24)) rom_1 (
    .addr(register_5_1_rd),
    .data({rom_1_data[23:19], INTACK, rom_1_data[17:16], DATAMUX, ARMUX, PCMUX, MUX, PCINC, SP_plus, SP_minus, ZFPOP, ZFLD, INTLD, MEMLD, REGLD, PCLD, IRLD}),
    .sel(pull_resistor_1_node));
  and and_2 (and_2_out, ~rom_1_data[19], ~rom_1_data[20], ~rom_1_data[21], ~rom_1_data[22], ~rom_1_data[23]);  // AND_Gate
  S_R_Flip_Flop s_r_ff_1 (
    .S(rom_1_data[17]), .R(rom_1_data[16]), .clk(clk), .en(pull_resistor_1_node), .Q(s_r_ff_1_q));  // open: clr
  and and_3 (and_3_out, and_2_out, s_r_ff_1_q, INT);
  or or_1 (or_1_out[0], and_3_out, and_4_out, and_5_out);
  and and_4 (and_4_out, ~and_1_out, IRLD);  // AND_Gate
  and and_5 (and_5_out, Z, IRLD);
  or or_2 (or_1_out[1], ~IRLD, and_3_out);  // OR_Gate

  // Notes on the sheet:
  //   contents of rom_1 (hex, n*v repeats v):
  //   201 604 1404 1008 2 2 0 24 2088 880100 608a 900100 20000 10000 780100 802140 2802 2404 2802 a16088
  //   aca098 3802
endmodule

module Register_5 (
  input  [4:0] ld,
  input  en,
  input  clk,
  output [4:0] rd
);

  D_Flip_Flop d_ff_1 (.D(ld[4]), .clk(clk), .Q(rd[4]), .en(en));  // open: clr
  D_Flip_Flop d_ff_2 (.D(ld[2]), .clk(clk), .Q(rd[2]), .en(en));  // open: clr
  D_Flip_Flop d_ff_3 (.D(ld[3]), .clk(clk), .Q(rd[3]), .en(en));  // open: clr
  D_Flip_Flop d_ff_4 (.D(ld[1]), .clk(clk), .Q(rd[1]), .en(en));  // open: clr
  D_Flip_Flop d_ff_5 (.D(ld[0]), .clk(clk), .Q(rd[0]), .en(en));  // open: clr
endmodule

module Interrupt_Controller (
  input  IRQ0,
  input  IRQ1,
  input  IRQ2,
  input  IRQ3,
  input  IRQ4,
  input  IRQ5,
  input  IRQ6,
  input  IRQ7,
  input  INTACK,
  output [2:0] INTV,
  output INT
);

  wire d_ff_1_q, d_ff_2_q, d_ff_3_q, d_ff_4_q, d_ff_5_q, d_ff_6_q, d_ff_7_q, d_ff_8_q, demultiplexer_1_out0,
       demultiplexer_1_out1, demultiplexer_1_out2, demultiplexer_1_out3, demultiplexer_1_out4,
       demultiplexer_1_out5, demultiplexer_1_out6, demultiplexer_1_out7, pull_resistor_1_node,
       pull_resistor_2_node;
  wire [2:0] priority_encoder_1_out;

  Pull_Resistor #(.pull(1)) pull_resistor_1 (.node(pull_resistor_1_node));
  D_Flip_Flop d_ff_1 (
    .D(pull_resistor_1_node), .clk(IRQ0), .Q(d_ff_1_q), .en(pull_resistor_1_node), .clr(demultiplexer_1_out0));
  D_Flip_Flop d_ff_2 (
    .D(pull_resistor_1_node), .clk(IRQ1), .Q(d_ff_2_q), .en(pull_resistor_1_node), .clr(demultiplexer_1_out1));
  D_Flip_Flop d_ff_3 (
    .D(pull_resistor_1_node), .clk(IRQ2), .Q(d_ff_3_q), .en(pull_resistor_1_node), .clr(demultiplexer_1_out2));
  D_Flip_Flop d_ff_4 (
    .D(pull_resistor_1_node), .clk(IRQ3), .Q(d_ff_4_q), .en(pull_resistor_1_node), .clr(demultiplexer_1_out3));
  D_Flip_Flop d_ff_5 (
    .D(pull_resistor_1_node), .clk(IRQ4), .Q(d_ff_5_q), .en(pull_resistor_1_node), .clr(demultiplexer_1_out4));
  D_Flip_Flop d_ff_6 (
    .D(pull_resistor_1_node), .clk(IRQ5), .Q(d_ff_6_q), .en(pull_resistor_1_node), .clr(demultiplexer_1_out5));
  D_Flip_Flop d_ff_7 (
    .D(pull_resistor_1_node), .clk(IRQ6), .Q(d_ff_7_q), .en(pull_resistor_1_node), .clr(demultiplexer_1_out6));
  D_Flip_Flop d_ff_8 (
    .D(pull_resistor_1_node), .clk(IRQ7), .Q(d_ff_8_q), .en(pull_resistor_1_node), .clr(demultiplexer_1_out7));
  Demultiplexer #(.select(3), .enable("false")) demultiplexer_1 (
    .out0(demultiplexer_1_out0), .out1(demultiplexer_1_out1), .out2(demultiplexer_1_out2),
    .out3(demultiplexer_1_out3), .out4(demultiplexer_1_out4), .out5(demultiplexer_1_out5),
    .out6(demultiplexer_1_out6), .out7(demultiplexer_1_out7), .in(INTACK), .sel(INTV));
  Priority_Encoder priority_encoder_1 (
    .in0(d_ff_1_q), .in1(d_ff_2_q), .in2(d_ff_3_q), .in3(d_ff_4_q), .in4(d_ff_5_q), .in5(d_ff_6_q),
    .in6(d_ff_7_q), .in7(d_ff_8_q), .out(priority_encoder_1_out), .en_in(pull_resistor_2_node), .gs(INT));  // open: en_out
  Register_3 register_3_1 (.ld(priority_encoder_1_out), .en(pull_resistor_2_node), .clk(INTACK), .rd(INTV));
  Pull_Resistor #(.pull(1)) pull_resistor_2 (.node(pull_resistor_2_node));
endmodule

module Register_3 (
  input  [2:0] ld,
  input  en,
  input  clk,
  output [2:0] rd
);

  D_Flip_Flop d_ff_1 (.D(ld[2]), .clk(clk), .Q(rd[2]), .en(en));  // open: clr
  D_Flip_Flop d_ff_2 (.D(ld[0]), .clk(clk), .Q(rd[0]), .en(en));  // open: clr
  D_Flip_Flop d_ff_3 (.D(ld[1]), .clk(clk), .Q(rd[1]), .en(en));  // open: clr
endmodule

module Interrupt_Register (
  input  [2:0] INTV,
  input  INTLD,
  input  clk,
  output [11:0] ISR
);

  wire [11:0] adder_1_out, bit_extender_1_out;

  assign bit_extender_1_out = {{9{1'b0}}, INTV};  // Bit_Extender bit_extender_1
  Register_12 register_12_1 (.ld(adder_1_out), .en(INTLD), .clk(clk), .rd(ISR));
  Adder #(.width(12)) adder_1 (.a(12'h7f0), .b(bit_extender_1_out), .out(adder_1_out));  // open: cin, cout
endmodule

module Switch_Adapter (
  input  en,
  input  addr,
  input  [15:0] ldsr,
  input  lddr,
  input  clk,
  output [15:0] rd
);

  wire and_1_out, Data_Register_q, multiplexer_1_out, pull_resistor_1_node, Status_Register_q, xor_1_out;

  and and_1 (and_1_out, addr, en, ~ldsr[0]);  // AND_Gate
  Pull_Resistor #(.pull(1)) pull_resistor_1 (.node(pull_resistor_1_node));
  S_R_Flip_Flop Status_Register (
    .S(xor_1_out), .R(and_1_out), .clk(clk), .en(pull_resistor_1_node), .Q(Status_Register_q));  // open: clr
  D_Flip_Flop Data_Register (.D(lddr), .clk(clk), .Q(Data_Register_q), .en(pull_resistor_1_node));  // open: clr
  xor xor_1 (xor_1_out, lddr, Data_Register_q);
  assign rd = {{15{1'b0}}, multiplexer_1_out};  // Bit_Extender bit_extender_1
  Multiplexer #(.enable("false")) multiplexer_1 (
    .in0(Data_Register_q), .in1(Status_Register_q), .out(multiplexer_1_out), .sel(addr));
endmodule

module Register_4 (
  input  [3:0] ld,
  input  en,
  input  clk,
  output [3:0] rd
);

  D_Flip_Flop d_ff_1 (.D(ld[3]), .clk(clk), .Q(rd[3]), .en(en));  // open: clr
  D_Flip_Flop d_ff_2 (.D(ld[2]), .clk(clk), .Q(rd[2]), .en(en));  // open: clr
  D_Flip_Flop d_ff_3 (.D(ld[1]), .clk(clk), .Q(rd[1]), .en(en));  // open: clr
  D_Flip_Flop d_ff_4 (.D(ld[0]), .clk(clk), .Q(rd[0]), .en(en));  // open: clr
endmodule

module Timer (
  output [15:0] t,
  output IRQ
);

  wire clock_1_out, pull_resistor_1_node;
  wire [11:0] adder_1_out, Clock_Divider_rd;
  wire [15:0] adder_2_out;

  Register_12 Clock_Divider (.ld(adder_1_out), .en(pull_resistor_1_node), .clk(clock_1_out), .rd(Clock_Divider_rd));
  Pull_Resistor #(.pull(1)) pull_resistor_1 (.node(pull_resistor_1_node));
  Clock clock_1 (.out(clock_1_out));
  Adder #(.width(12)) adder_1 (.a(12'h1), .b(Clock_Divider_rd), .out(adder_1_out));  // open: cin, cout
  Register_16 Timer (.ld(adder_2_out), .en(pull_resistor_1_node), .clk(IRQ), .rd(t));
  and and_1 (IRQ, Clock_Divider_rd[0], Clock_Divider_rd[1], Clock_Divider_rd[2], Clock_Divider_rd[3], Clock_Divider_rd[4], Clock_Divider_rd[5], Clock_Divider_rd[6], Clock_Divider_rd[7]);
  Adder #(.width(16)) adder_2 (.a(16'h1), .b(t), .out(adder_2_out));  // open: cin, cout

  // Notes on the sheet:
  //   Although theoretically, 12-bit clock divider with 4.1 KHz clock must generate a 1Hz clock pulse(pulses once each second), this configuration produces the best results on my machine
endmodule

module S_R_Flip_Flop (
  input  S,
  input  R,
  input  clk,
  input  en,
  input  clr,
  output Q
);

  S_R_Flip_Flop_part s_r_ff_1 (.S(S), .clk(clk), .R(R), .Q(Q), .reset(clr), .en(en));  // open: Qn, preset
endmodule

module SwitchBoard_4_Adapter (
  input  en,
  input  addr,
  input  [15:0] ldsr,
  input  [3:0] lddr,
  input  clk,
  output [15:0] rd
);

  wire and_1_out, or_1_out, pull_resistor_1_node, Status_Register_q, xor_1_out, xor_2_out, xor_3_out,
       xor_4_out;
  wire [3:0] bit_extender_1_out, Data_Register_rd, multiplexer_1_out;

  and and_1 (and_1_out, addr, en, ~ldsr[0]);  // AND_Gate
  or or_1 (or_1_out, xor_1_out, xor_2_out, xor_3_out, xor_4_out);
  xor xor_1 (xor_1_out, lddr[3], Data_Register_rd[3]);
  xor xor_2 (xor_2_out, lddr[2], Data_Register_rd[2]);
  S_R_Flip_Flop Status_Register (
    .S(or_1_out), .R(and_1_out), .clk(clk), .en(pull_resistor_1_node), .Q(Status_Register_q));  // open: clr
  Pull_Resistor #(.pull(1)) pull_resistor_1 (.node(pull_resistor_1_node));
  Register_4 Data_Register (.ld(lddr), .en(pull_resistor_1_node), .clk(clk), .rd(Data_Register_rd));
  xor xor_3 (xor_3_out, lddr[1], Data_Register_rd[1]);
  xor xor_4 (xor_4_out, lddr[0], Data_Register_rd[0]);
  assign bit_extender_1_out = {{3{1'b0}}, Status_Register_q};  // Bit_Extender bit_extender_1
  Multiplexer #(.width(4), .enable("false")) multiplexer_1 (
    .in0(Data_Register_rd), .in1(bit_extender_1_out), .out(multiplexer_1_out), .sel(addr));
  assign rd = {{12{1'b0}}, multiplexer_1_out};  // Bit_Extender bit_extender_2
endmodule

module _4_7_Segment_Adapter (
  input  [15:0] ld,
  input  en,
  input  addr,
  input  clk,
  output [3:0] gfab1,
  output [2:0] edc1,
  output [3:0] gfab2,
  output [2:0] edc2,
  output [3:0] gfab3,
  output [2:0] edc3,
  output [3:0] gfab4,
  output [2:0] edc4,
  output [15:0] rd
);

  wire demultiplexer_1_out0, demultiplexer_1_out1;
  wire [15:0] register_16_1_rd;

  Demultiplexer #(.enable("false")) demultiplexer_1 (
    .out0(demultiplexer_1_out0), .out1(demultiplexer_1_out1), .in(en), .sel(addr));
  Register_16 register_16_1 (.ld(ld), .en(demultiplexer_1_out0), .clk(clk), .rd(register_16_1_rd));
  assign rd = demultiplexer_1_out1 ? 16'h1 : 16'bz;  // Controlled_Buffer controlled_buffer_1
  _7_Segment_Decimal_Adapter u_7_segment_decimal_adapter_1 (.num(register_16_1_rd[3:0]), .edc(edc1), .gfab(gfab1));
  _7_Segment_Decimal_Adapter u_7_segment_decimal_adapter_2 (.num(register_16_1_rd[7:4]), .edc(edc2), .gfab(gfab2));
  _7_Segment_Decimal_Adapter u_7_segment_decimal_adapter_3 (.num(register_16_1_rd[11:8]), .edc(edc3), .gfab(gfab3));
  _7_Segment_Decimal_Adapter u_7_segment_decimal_adapter_4 (.num(register_16_1_rd[15:12]), .edc(edc4), .gfab(gfab4));
endmodule

module Register_7 (
  input  [6:0] ld,
  input  en,
  input  clk,
  output [6:0] rd
);

  D_Flip_Flop d_ff_1 (.D(ld[6]), .clk(clk), .Q(rd[6]), .en(en));  // open: clr
  D_Flip_Flop d_ff_2 (.D(ld[4]), .clk(clk), .Q(rd[4]), .en(en));  // open: clr
  D_Flip_Flop d_ff_3 (.D(ld[5]), .clk(clk), .Q(rd[5]), .en(en));  // open: clr
  D_Flip_Flop d_ff_4 (.D(ld[3]), .clk(clk), .Q(rd[3]), .en(en));  // open: clr
  D_Flip_Flop d_ff_5 (.D(ld[2]), .clk(clk), .Q(rd[2]), .en(en));  // open: clr
  D_Flip_Flop d_ff_6 (.D(ld[1]), .clk(clk), .Q(rd[1]), .en(en));  // open: clr
  D_Flip_Flop d_ff_7 (.D(ld[0]), .clk(clk), .Q(rd[0]), .en(en));  // open: clr
endmodule

module clz_16 (
  input  [15:0] D,
  output [15:0] Q
);

  wire and_1_out, and_2_out, and_3_out, and_4_out, and_5_out, and_6_out, and_7_out, and_8_out, and_9_out,
       and_10_out, and_11_out, and_12_out, and_13_out, and_14_out, and_15_out, or_1_out, or_2_out, or_3_out,
       or_4_out, or_5_out, or_6_out, or_7_out, or_8_out, or_9_out, or_10_out, or_11_out, or_12_out,
       or_13_out, or_14_out, or_15_out, or_17_out, or_18_out, or_19_out, or_21_out;
  wire [4:0] or_23_out;

  or or_1 (or_1_out, D[15], D[14]);
  or or_2 (or_2_out, or_1_out, D[13]);
  or or_3 (or_3_out, or_2_out, D[12]);
  or or_4 (or_4_out, or_3_out, D[11]);
  or or_5 (or_5_out, or_4_out, D[10]);
  or or_6 (or_6_out, or_5_out, D[9]);
  or or_7 (or_7_out, or_6_out, D[8]);
  or or_8 (or_8_out, or_7_out, D[7]);
  or or_9 (or_9_out, or_8_out, D[6]);
  or or_10 (or_10_out, or_9_out, D[5]);
  or or_11 (or_11_out, or_10_out, D[4]);
  or or_12 (or_12_out, or_11_out, D[3]);
  or or_13 (or_13_out, or_12_out, D[2]);
  or or_14 (or_14_out, or_13_out, D[1]);
  or or_15 (or_15_out, or_14_out, D[0]);
  and and_1 (and_1_out, ~D[15], or_1_out);  // AND_Gate
  and and_2 (and_2_out, ~or_1_out, or_2_out);  // AND_Gate
  and and_3 (and_3_out, ~or_2_out, or_3_out);  // AND_Gate
  and and_4 (and_4_out, ~or_3_out, or_4_out);  // AND_Gate
  and and_5 (and_5_out, ~or_4_out, or_5_out);  // AND_Gate
  and and_6 (and_6_out, ~or_5_out, or_6_out);  // AND_Gate
  and and_7 (and_7_out, ~or_6_out, or_7_out);  // AND_Gate
  and and_8 (and_8_out, ~or_7_out, or_8_out);  // AND_Gate
  and and_9 (and_9_out, ~or_8_out, or_9_out);  // AND_Gate
  and and_10 (and_10_out, ~or_9_out, or_10_out);  // AND_Gate
  and and_11 (and_11_out, ~or_10_out, or_11_out);  // AND_Gate
  and and_12 (and_12_out, ~or_11_out, or_12_out);  // AND_Gate
  and and_13 (and_13_out, ~or_12_out, or_13_out);  // AND_Gate
  and and_14 (and_14_out, ~or_13_out, or_14_out);  // AND_Gate
  and and_15 (and_15_out, ~or_14_out, or_15_out);  // AND_Gate
  and and_16 (or_23_out[4], ~or_15_out, ~or_15_out);  // AND_Gate
  or or_16 (or_23_out[3], or_17_out, or_18_out, and_9_out, and_8_out);
  or or_17 (or_17_out, or_19_out, and_13_out, and_12_out);
  or or_18 (or_18_out, and_11_out, and_10_out);
  or or_19 (or_19_out, and_15_out, and_14_out);
  or or_20 (or_23_out[2], or_17_out, or_21_out, and_5_out, and_4_out);
  or or_21 (or_21_out, and_7_out, and_6_out);
  assign Q = {{11{1'b0}}, or_23_out};  // Bit_Extender bit_extender_1
  or or_22 (or_23_out[1], and_3_out, and_2_out, or_19_out, or_18_out, or_21_out);
  or or_23 (or_23_out[0], and_1_out, and_15_out, and_13_out, and_11_out, and_9_out, and_7_out, and_5_out, and_3_out);
endmodule

module _7_Segment_Decimal_Adapter (
  input  [3:0] num,
  output [2:0] edc,
  output [3:0] gfab
);

  wire and_1_out, and_2_out, and_3_out, and_4_out, and_5_out, and_6_out, and_7_out, and_8_out, and_9_out,
       and_10_out, and_11_out, and_12_out, and_13_out, and_14_out, and_15_out, and_16_out, and_17_out,
       and_18_out, and_19_out, and_20_out, and_21_out, and_22_out, and_23_out, not_1_out, not_2_out,
       not_3_out, not_4_out, not_5_out, not_6_out, not_7_out, not_8_out, not_9_out, not_10_out, not_11_out,
       not_12_out, not_13_out, not_14_out, not_15_out, not_16_out, not_17_out, not_18_out, not_19_out,
       not_20_out, not_21_out, not_22_out, not_23_out, not_24_out, not_25_out, not_26_out, not_27_out,
       not_28_out, not_29_out;

  not not_1 (not_1_out, num[2]);
  not not_2 (not_2_out, num[0]);
  not not_3 (not_3_out, num[3]);
  not not_4 (not_4_out, num[2]);
  not not_5 (not_5_out, num[3]);
  not not_6 (not_6_out, num[1]);
  not not_7 (not_7_out, num[0]);
  not not_8 (not_8_out, num[2]);
  not not_9 (not_9_out, num[1]);
  not not_10 (not_10_out, num[3]);
  not not_11 (not_11_out, num[2]);
  not not_12 (not_12_out, num[1]);
  not not_13 (not_13_out, num[3]);
  not not_14 (not_14_out, num[3]);
  not not_15 (not_15_out, num[2]);
  not not_16 (not_16_out, num[0]);
  not not_17 (not_17_out, num[2]);
  not not_18 (not_18_out, num[0]);
  not not_19 (not_19_out, num[1]);
  not not_20 (not_20_out, num[2]);
  not not_21 (not_21_out, num[0]);
  not not_22 (not_22_out, num[0]);
  not not_23 (not_23_out, num[1]);
  not not_24 (not_24_out, num[0]);
  not not_25 (not_25_out, num[1]);
  not not_26 (not_26_out, num[0]);
  not not_27 (not_27_out, num[2]);
  not not_28 (not_28_out, num[1]);
  not not_29 (not_29_out, num[0]);
  and and_1 (and_1_out, not_1_out, not_2_out);
  and and_2 (and_2_out, num[2], num[0]);
  and and_3 (and_3_out, not_3_out, not_4_out);
  and and_4 (and_4_out, not_5_out, not_6_out, not_7_out);
  and and_5 (and_5_out, not_8_out, not_9_out);
  and and_6 (and_6_out, not_10_out, num[1], num[0]);
  and and_7 (and_7_out, not_11_out, not_12_out);
  and and_8 (and_8_out, not_13_out, num[0]);
  and and_9 (and_9_out, not_14_out, num[2]);
  and and_10 (and_10_out, not_15_out, not_16_out);
  and and_11 (and_11_out, not_17_out, num[1]);
  and and_12 (and_12_out, num[1], not_18_out);
  and and_13 (and_13_out, num[2], not_19_out, num[0]);
  and and_14 (and_14_out, not_20_out, not_21_out);
  and and_15 (and_15_out, num[1], not_22_out);
  and and_16 (and_16_out, num[3], num[1]);
  and and_17 (and_17_out, num[3], num[2]);
  and and_18 (and_18_out, not_23_out, not_24_out);
  and and_19 (and_19_out, num[2], not_25_out);
  and and_20 (and_20_out, num[2], not_26_out);
  and and_21 (and_21_out, not_27_out, num[1]);
  and and_22 (and_22_out, num[2], not_28_out);
  and and_23 (and_23_out, num[2], not_29_out);
  or or_1 (gfab[1], and_1_out, num[1], and_2_out, num[3]);
  or or_2 (gfab[0], and_3_out, and_4_out, and_5_out, and_6_out);
  or or_3 (edc[0], and_7_out, and_8_out, and_9_out);
  or or_4 (edc[1], and_10_out, and_11_out, and_12_out, and_13_out, num[3]);
  or or_5 (edc[2], and_14_out, and_15_out, and_16_out, and_17_out);
  or or_6 (gfab[2], and_18_out, and_19_out, and_20_out, num[3]);
  or or_7 (gfab[3], and_21_out, and_22_out, and_23_out, num[3]);
endmodule

module Switch_Adapter_With_Memory (
  input  en,
  input  addr,
  input  [15:0] ldsr,
  input  clk,
  input  lddr,
  output [15:0] rd
);

  wire and_1_out, and_2_out, Data_Register_q, multiplexer_1_out, or_1_out, pull_resistor_1_node,
       Status_Register_q;

  and and_1 (and_1_out, addr, en, ~ldsr[0]);  // AND_Gate
  Pull_Resistor #(.pull(1)) pull_resistor_1 (.node(pull_resistor_1_node));
  S_R_Flip_Flop Status_Register (
    .S(and_2_out), .R(and_1_out), .clk(clk), .en(pull_resistor_1_node), .Q(Status_Register_q));  // open: clr
  or or_1 (or_1_out, and_1_out, ~Status_Register_q);  // OR_Gate
  D_Flip_Flop Data_Register (.D(lddr), .clk(clk), .Q(Data_Register_q), .en(or_1_out));  // open: clr
  and and_2 (and_2_out, lddr, ~Data_Register_q);  // AND_Gate
  assign rd = {{15{1'b0}}, multiplexer_1_out};  // Bit_Extender bit_extender_1
  Multiplexer #(.enable("false")) multiplexer_1 (
    .in0(Data_Register_q), .in1(Status_Register_q), .out(multiplexer_1_out), .sel(addr));
endmodule
